# Fritzing sketch HomeSecuripy (saved by Fritzing 0.8.7b)

parts:
  Raspberry_Pi_Zero1 = Raspberry Pi Zero
  U1 = TCM8240MD [package=tcm8240md]  # not connected
  SPKR1 = Loudspeaker
  PIR1 = PIR sensor
  MIC1 = MAX4466 Electret Microphone Breakout Board

nets:
  N1: Raspberry_Pi_Zero1.GIPO22, MIC1.out
  GND: Raspberry_Pi_Zero1.GND, PIR1.GND, MIC1.GND
  N2: Raspberry_Pi_Zero1.GIPO16, PIR1.SIG
  N3: Raspberry_Pi_Zero1.GIPO18, SPKR1.pin2
  5V: Raspberry_Pi_Zero1.5V, PIR1.VDD, MIC1.VCC

notes:
  Place Pi Camera in Camera Slot

custom parts:
  MAX4466 Electret Microphone Breakout Board: MAX4466 Electrec Microphone Breakout Board
