# Fritzing sketch IA5 (saved by Fritzing 0.9.5d)
breadboards: 1

parts:
  MCU1 = Raspberry Pi Zero
  Part1 = Arduino Nano (Rev3.0) (ICSP)
  Part2 = Logic Level Converter

nets:
  N1: MCU1.pin_2, Part1.VIN
  N2: MCU1.pin_34, MCU1.pin_39, Part1.GND
  N3: Part1.D1/TX, Part2.RX_HV
  N4: Part1.D0/RX, Part2.TX_HV
  N5: Part1.5V, Part2.HV
