# Fritzing sketch Lab3 (saved by Fritzing 0.9.5d)
breadboards: 1

parts:
  MCU1 = Raspberry Pi Zero
  LED1 = smd LED [color="Red (633nm)" package="0603 [SMD]"]
  LED2 = smd LED [color="White (4500K)" package="0603 [SMD]"]
  LED3 = smd LED [color="Green (555nm)" package="1206 [SMD]"]
  LED4 = smd LED [color="White (4500K)" package="1206 [SMD]"]
  LED5 = smd LED [color="Red (633nm)" package="1206 [SMD]"]
  R1 = Resistor [tolerance=±5% resistance=470 package="1206 [SMD]"]
  R2 = Resistor [tolerance=±5% resistance=470 package="1206 [SMD]"]
  R3 = Resistor [tolerance=±5% resistance=470 package="1206 [SMD]"]
  R4 = Resistor [tolerance=±5% resistance=470 package="1206 [SMD]"]
  R5 = Resistor [tolerance=±5% resistance=470 package="1206 [SMD]"]
  S1 = Momentary Switch [package=ksa_sealed_tac_switch]
  S2 = Momentary Switch [package=ksa_sealed_tac_switch]
  S3 = Momentary Switch [package=ksa_sealed_tac_switch]
  LED6 = smd LED [color="Yellow (585nm)" package="1206 [SMD]"]
  R6 = Resistor [tolerance=±5% resistance=470 package="1206 [SMD]"]

nets:
  N1: MCU1.pin_6, MCU1.pin_20, MCU1.pin_39, R1.Pin_0, R2.Pin_0, R3.Pin_0, R4.Pin_0, R5.Pin_0, S3.1, R6.Pin_0
  N2: MCU1.pin_13, S3.2
  N3: MCU1.pin_15, LED6.anode
  N4: MCU1.pin_29, LED1.anode
  N5: MCU1.pin_31, LED2.anode
  N6: MCU1.pin_33, LED3.anode
  N7: MCU1.pin_35, LED4.anode
  N8: MCU1.pin_37, LED5.anode
  N9: MCU1.pin_38, S2.1
  N10: MCU1.pin_40, S1.1
  N11: LED1.cathode, R1.Pin_1
  N12: LED2.cathode, R2.Pin_1
  N13: LED3.cathode, R3.Pin_1
  N14: LED4.cathode, R4.Pin_1
  N15: LED5.cathode, R5.Pin_1
  N16: S1.2, S1.4, S2.2, S2.4
  N17: LED6.cathode, R6.Pin_1
