# Fritzing sketch Main Task 1 (saved by Fritzing 0.9.5d)
breadboards: 1

parts:
  Part1 = Arduino Nano (Rev3.0) (ICSP)
  R1 = Photocell (LDR) [package=THT]
  R2 = Resistor [tolerance=±5% resistance=220 package="0402 [SMD]"]

nets:
  N1: Part1.GND, R2.Pin_0
  N2: Part1.5V, R1.pin_0
  N3: Part1.A0, R1.pin_1, R2.Pin_1
