# Fritzing sketch Main Task 2 (saved by Fritzing 0.9.5d)
breadboards: 1

parts:
  Part1 = Arduino Nano (Rev3.0) (ICSP)
  R2 = Resistor [tolerance=±5% resistance=220 package="0402 [SMD]"]
  R3 = Temperature Sensor (Thermistor) [thermistor_type=NTC package=THT]
  C1 = Capacitor [package=cap-pth-small2]

nets:
  N1: Part1.GND, C1.2
  N2: Part1.5V, R3.pin_1
  N3: Part1.A0, R2.Pin_0, R3.pin_0
  N4: R2.Pin_1, C1.1
