# Fritzing sketch Main Task 1 (saved by Fritzing 0.9.5d)
breadboards: 1

parts:
  C1 = Electrolytic Capacitor [capacitance=10μF package="0605 [SMD, electrolytic]"]
  F1 = Resettable Fuse PTC [package=ptc]
  D1 = Rectifier Diode 10A [part_number=P1000K]  # not connected
  M1 = DC Motor
  MCU1 = Raspberry Pi Zero

nets:
  N1: C1.-, C1.+, F1.2, M1.pin_1, MCU1.pin_2, MCU1.pin_4
  N2: F1.1, M1.pin_2
