# Fritzing sketch Main Task 2 (saved by Fritzing 0.9.5d)
breadboards: 1

parts:
  MCU1 = Raspberry Pi Zero
  U1 = Sharp PC817 [package=THT]
  R1 = Resistor [tolerance=±5% resistance=470 package="0402 [SMD]"]
  BAT1 = BC9VPC [package=bc9vpc]
  Q1 = NPN-Transistor [package="TO92 [THT]"]
  R2 = Resistor [tolerance=±5% resistance=10k package="0402 [SMD]"]
  C1 = Electrolytic Capacitor [capacitance=10µF package="1010 [SMD, electrolytic]"]
  U2 = DIODE-ZENER [package=diode-zener]
  F1 = Resettable Fuse PTC [package=ptc]
  M1 = DC Motor

nets:
  N1: MCU1.pin_12, U1.Pin_1
  N2: MCU1.pin_20, MCU1.pin_34, R1.Pin_1
  N3: U1.Pin_2, R1.Pin_0
  N4: U1.Pin_4, BAT1.V+, F1.2
  N5: U1.Pin_3, Q1.B, R2.Pin_0
  N6: BAT1.V-, Q1.C, R2.Pin_1, C1.-
  N7: Q1.E, C1.+, M1.pin_2
  N8: U2.C, F1.1, M1.pin_1
