# Fritzing sketch Main Task 4 (saved by Fritzing 0.9.5d)
breadboards: 1

parts:
  MCU1 = Raspberry Pi Zero
  Part1 = Arduino Nano (Rev3.0) (ICSP)
  Part2 = Logic Level Converter
  R1 = Trimmer Potentiometer [maximum_resistance=10kΩ package=THT]
  R2 = Trimmer Potentiometer [maximum_resistance=10kΩ package=THT]

nets:
  N1: MCU1.pin_1, MCU1.pin_17, Part2.LV
  N2: MCU1.pin_2, MCU1.pin_4, R1.leg2, R2.leg2
  N3: MCU1.pin_8, Part2.TX_LV
  N4: MCU1.pin_10, Part2.RX_LV
  GND: MCU1.pin_34, MCU1.pin_38, MCU1.pin_39, Part1.GND, Part2.GND, R1.leg1, R2.leg1
  N5: Part1.D1/TX, Part2.RX_HV
  N6: Part1.D0/RX, Part2.TX_HV
  N7: Part1.5V, Part2.HV
  N8: Part1.A1, R2.wiper
  N9: Part1.A0, R1.wiper
