# Fritzing sketch Lab9 (saved by Fritzing 0.9.5d)
breadboards: 1

parts:
  MCU1 = Raspberry Pi Zero
  LED1 = LED - 5mm [color="Red (633nm)" package="5 mm [THT]"]
  LED2 = LED - 5mm [color="Yellow (585nm)" package="5 mm [THT]"]
  LED3 = LED - 5mm [color="Green (555nm)" package="5 mm [THT]"]
  R1 = Resistor [tolerance=±5% resistance=470 package="2010 [SMD]"]
  R2 = Resistor [tolerance=±5% resistance=470 package="2010 [SMD]"]
  R3 = Resistor [tolerance=±5% resistance=470 package="2010 [SMD]"]
  S1 = SWITCH-MOMENTARY-2 [package=tactile-pth-12mm]

nets:
  N1: MCU1.pin_6, MCU1.pin_30, MCU1.pin_34, LED1.cathode, LED2.cathode, LED3.cathode, S1.1
  N2: MCU1.pin_12, S1.2
  N3: MCU1.pin_18, R3.Pin_0
  N4: MCU1.pin_22, R2.Pin_0
  N5: MCU1.pin_32, R1.Pin_0
  N6: LED1.anode, R1.Pin_1
  N7: LED2.anode, R2.Pin_1
  N8: LED3.anode, R3.Pin_1
